# Fritzing sketch Breadboard Sketch (saved by Fritzing 0.7.10b)
breadboards: 1

parts:
  Arduino1 = Arduino
  R1 = Resistor [tolerance=±5% resistance=15k package=THT]
  RE1 = Rotary Encoder [package=THT]
  R2 = Photocell (LDR) [package=THT]
  LED1 = LED - 5mm [color="Infrared (880nm)" package="5 mm [THT]"]
  R3 = Resistor [tolerance=±5% resistance=100 package=THT]
  R4 = Resistor [tolerance=±5% resistance=27k package=THT]
  S1 = Pushbutton [package="[THT]"]

nets:
  N1: Arduino1.aref, RE1.EncoderPinA, S1.Pin_3, S1.Pin_4
  N2: Arduino1.GND, R1.Pin_0, LED1.cathode
  N3: Arduino1.D13, R3.Pin_0
  N4: Arduino1.D5, Arduino1.+5V, R2.pin_0
  N5: Arduino1.D4, S1.Pin_1, S1.Pin_2
  N6: Arduino1.D2, RE1.EncoderPinB
  N7: R1.Pin_1, R4.Pin_0
  N8: R2.pin_1, R4.Pin_1
  N9: LED1.anode, R3.Pin_1
